# Fritzing sketch PiezoServoUno (saved by Fritzing 0.9.2b)
circuit board: 3.03975cm x 3.66426cm

parts:
  part = Resistor [tolerance=±5% resistance=1M package=THT]
  Piezo_element = Piezo Speaker
  part_2 = Battery block 9V
  J1 = Basic Servo
  Part3 = Arduino Uno (Rev3) - ICSP

nets:
  N1: part.Pin_0, Piezo_element.pin2, Part3.A0
  GND: part.Pin_1, Piezo_element.pin1, part_2.-, J1.gnd, Part3.GND
  N2: part_2.+, Part3.VIN
  VCC: J1.vcc, Part3.5V
  N3: J1.pulse, Part3.D3_PWM
